# Fritzing sketch Solar_power (saved by Fritzing 0.7.11b)
breadboards: 1

parts:
  SLR_PNL = female pin header, 2 pins [form="♀ (female)"]
  BATT = female pin header, 2 pins [form="♀ (female)"]
  POW = female pin header, 2 pins [form="♀ (female)"]
  D1 = Schottky Diode [part_number=1N5817 package="300 mil [THT]"]
  D3 = Schottky Diode [part_number=1N5817 package="300 mil [THT]"]
  D2 = Schottky Diode [part_number=1N5817 package="300 mil [THT]"]

nets:
  N1: SLR_PNL.pin1, D1.anode, D3.anode
  N2: SLR_PNL.pin2, BATT.pin2, POW.pin2
  N3: BATT.pin1, D3.cathode, D2.anode
  N4: POW.pin1, D1.cathode, D2.cathode
